# Fritzing sketch bat meter (saved by Fritzing 0.9.3b)
breadboards: 2

parts:
  Bauteil1 = Arduino Micro (Rev3)  # not connected
  D1 = LED_BARGRAPH_10 [package=led_bargaph_10]
  R1 = Resistor [tolerance=±5% resistance=220 package=THT]
  U1 = LIPO-110mAh [package=lipo-110]
  U2 = LM5007 [package=msop-8-ep]  # not connected
  U2_2 = LMZ14203 [package=to-pmod-7]  # not connected
  U2_3 = LM5007 [package=msop-8-ep]  # not connected
  U2_4 = DC-DC_CONVERTER [package=dc-dc_converter]  # not connected
  R2 = Resistor [tolerance=±5% resistance=220 package=THT]

nets:
  N1: D1.J_C, D1.I_C, D1.H_C, D1.G_C, D1.F_C, D1.E_C, D1.D_C, D1.C_C, D1.B_C, D1.A_C, R1.Pin_1
  N2: U1.-, R2.Pin_0
